# Fritzing sketch MicroTeclado (saved by Fritzing 1.0.2b)
breadboards: 1

parts:
  LED1 = RGB LED (com. cathode, rgb) [color="Red (633nm)" current=0.030A package="5 mm [THT]"]
  LED2 = RGB LED (com. cathode, rgb) [color="Red (633nm)" current=0.030A package="5 mm [THT]"]
  LED3 = RGB LED (com. cathode, rgb) [color="Red (633nm)" current=0.030A package="5 mm [THT]"]
  LED4 = RGB LED (com. cathode, rgb) [color="Red (633nm)" current=0.030A package="5 mm [THT]"]
  LED5 = RGB LED (com. cathode, rgb) [color="Red (633nm)" current=0.030A package="5 mm [THT]"]
  LED6 = RGB LED (com. cathode, rgb) [color="Red (633nm)" current=0.030A package="5 mm [THT]"]
  LED7 = RGB LED (com. cathode, rgb) [color="Red (633nm)" current=0.030A package="5 mm [THT]"]
  LED8 = RGB LED (com. cathode, rgb) [color="Red (633nm)" current=0.030A package="5 mm [THT]"]
  LED9 = RGB LED (com. cathode, rgb) [color="Red (633nm)" current=0.030A package="5 mm [THT]"]
  LED10 = RGB LED (com. cathode, rgb) [color="Red (633nm)" current=0.030A package="5 mm [THT]"]
  LED11 = RGB LED (com. cathode, rgb) [color="Red (633nm)" current=0.030A package="5 mm [THT]"]
  LED12 = RGB LED (com. cathode, rgb) [color="Red (633nm)" current=0.030A package="5 mm [THT]"]
  Componente1 = Arduino Mega Proto Shield (v6)
  S1 = Pushbutton [package=THT]
  S2 = Pushbutton [package=THT]
  S3 = Pushbutton [package=THT]
  S4 = Pushbutton [package=THT]
  S5 = Pushbutton [package=THT]
  S6 = Pushbutton [package=THT]
  S7 = Pushbutton [package=THT]
  S8 = Pushbutton [package=THT]
  S9 = Pushbutton [package=THT]
  S10 = Pushbutton [package=THT]
  S11 = Pushbutton [package=THT]
  S12 = Pushbutton [package=THT]

nets:
  N1: LED1.red_anode, Componente1.D47
  N2: LED1.common_cathode, LED2.common_cathode, LED3.common_cathode, LED4.common_cathode, LED5.common_cathode, LED6.common_cathode, LED7.common_cathode, LED8.common_cathode, LED9.common_cathode, LED10.common_cathode, LED11.common_cathode, LED12.common_cathode, Componente1.GND, S1.leg1, S2.leg1, S3.leg1, S4.leg1, S5.leg1, S6.leg1, S7.leg1, S8.leg1, S9.leg1, S10.leg1, S11.leg1, S12.leg1
  N3: LED1.green_anode, Componente1.D5
  N4: LED2.red_anode, Componente1.D49
  N5: LED2.green_anode, Componente1.D4
  N6: LED3.red_anode, Componente1.D45
  N7: LED3.green_anode, Componente1.D6
  N8: LED4.red_anode, Componente1.D43
  N9: LED4.green_anode, Componente1.D7
  N10: LED5.red_anode, Componente1.D51
  N11: LED5.green_anode, Componente1.D3
  N12: LED6.red_anode, Componente1.D53
  N13: LED6.green_anode, Componente1.D2
  N14: LED7.red_anode, Componente1.D37
  N15: LED7.green_anode, Componente1.D10
  N16: LED8.red_anode, Componente1.D35
  N17: LED8.green_anode, Componente1.D11
  N18: LED9.red_anode, Componente1.D31
  N19: LED9.green_anode, Componente1.D13
  N20: LED10.red_anode, Componente1.D33
  N21: LED10.green_anode, Componente1.D12
  N22: LED11.red_anode, Componente1.D41
  N23: LED11.green_anode, Componente1.D8
  N24: LED12.red_anode, Componente1.D39
  N25: LED12.green_anode, Componente1.D9
  N26: Componente1.D22, S1.leg0
  N27: Componente1.D24, S2.leg0
  N28: Componente1.D26, S3.leg0
  N29: Componente1.D28, S4.leg0
  N30: Componente1.D30, S5.leg0
  N31: Componente1.D32, S6.leg0
  N32: Componente1.D34, S7.leg0
  N33: Componente1.D36, S8.leg0
  N34: Componente1.D38, S9.leg0
  N35: Componente1.D40, S10.leg0
  N36: Componente1.D42, S11.leg0
  N37: Componente1.D44, S12.leg0

notes:
  C
  C*
  D
  D*
  E
  F
  F*
  G
  G*
  A
  A*
  B
